# Fritzing sketch 8266+dht11 (saved by Fritzing 0.9.4)

parts:
  U2 = NodeMCU V3.0
  DHT11_2 = DHT11 module

nets:
  N1: U2.D4, DHT11_2.DATA
  3V3: U2.3V3, DHT11_2.VCC
  GND: U2.GND, DHT11_2.GND

custom parts:
  NodeMCU V3.0: ESP8266 based NodeMCU
  DHT11 module: DHT11 black pcb module
