# Fritzing sketch esp8266+rfm95+dht11+battery (saved by Fritzing 0.9.4)

parts:
  U1 = NodeMCU V3.0
  RFM95W1 = RFM95W LoRa Module
  R1 = Resistor [tolerance=±5% resistance=220 package=THT]
  DHT11_1 = DHT11 module
  BAT2 = 18650 battery holder [package=battery-18650-kit]

nets:
  N1: U1.D0, RFM95W1.6_RESET
  N2: U1.D1, RFM95W1.14_DIO0
  N3: U1.D2, RFM95W1.15_DIO1
  3V3: U1.3V3, RFM95W1.13_3.3V, R1.Pin_0, DHT11_1.VCC, BAT2.+
  N4: U1.GND#6, U1.GND#13, U1.GND#16, RFM95W1.10_GND, DHT11_1.GND
  N5: U1.D6, RFM95W1.2_MISO
  N6: U1.D7, RFM95W1.3_MOSI
  N7: U1.D8, RFM95W1.5_NSS_(CS)
  N8: U1.RX, DHT11_1.DATA
  N9: U1.TX, R1.Pin_1
  N10: U1.GND#41, BAT2.-

custom parts:
  NodeMCU V3.0: ESP8266 based NodeMCU
  RFM95W LoRa Module: RF Transceiver by Hope RF. Well supported Arduino libraries are available. This Low Power Long Range Transceiver Module for the frequencies 868MHz and 915MHz and it is also available in other versions.
  DHT11 module: DHT11 black pcb module
  18650 battery holder: 18650 Battery Holder
